# Fritzing sketch 01warning_device (saved by Fritzing 0.9.3b)
breadboards: 1

parts:
  U3 = ESP32S-HiLetgo [part_number=ESP32S-HiLetgo]
  LED2 = LED - 3mm [color="Red (633nm)" package="3 mm [THT]"]
  LED3 = LED - 3mm [color="Blue (430nm)" package="3 mm [THT]"]

nets:
  N1: U3.GND, LED2.cathode, LED3.cathode
  N2: U3.GPIO2, LED3.anode
  N3: U3.GPIO16, LED2.anode

custom parts:
  ESP32S-HiLetgo: HiLetgo ESP-WROOM-32 ESP32 ESP-32S Development Board 2.4GHz Dual-Mode WiFi + Bluetooth Dual Cores Microcontroller The ESP32 integrated with Antenna switches, RF Balun, power amplifiers, low-noise amplifiers, filters, and management modules, and the entire solution occupies the least area of PCB. 2.4 GHz Wi-Fi plus Bluetooth dual-mode chip, with TSMC Ultra-low power consumption 40nm technology,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

// code stored in the sketch: sketch_oct02a.ino
void setup() {
  // put your setup code here, to run once:
  Serial.begin(115200);
  pinMode(2, OUTPUT);
  pinMode(16, OUTPUT);  
  Serial.println("Start touch work");
}

void alarm(){ // shine two LEDs 
  digitalWrite(2, HIGH);
  delay(50);
  digitalWrite(16, LOW);
  delay(50);
  digitalWrite(2, LOW);
  delay(50);
  digitalWrite(16, HIGH);
  delay(50);
}

void loop() {  
  Serial.println(touchRead(T3)); // print out resistance number
  if(touchRead(T3) < 40){ // trigger alarm() when touch the wire
    Serial.println("detected hand");
    alarm();
  }
  else{ // turn off light
    Serial.println("clear");
    digitalWrite(2, LOW);
    digitalWrite(16, LOW);
  }
}
