# Fritzing sketch HW03_12 (saved by Fritzing 0.9.3b)
breadboards: 2

parts:
  U2 = ESP32S-HiLetgo [part_number=ESP32S-HiLetgo]
  LED1 = smd LED [color="Red (633nm)" package="0603 [SMD]"]
  LED2 = smd LED [color="Blue (470nm)" package="0603 [SMD]"]
  SERVO1 = Tower Pro SG90 servo [part_number=101246]
  S1 = Momentary Switch [package=ksa_sealed_tac_switch]
  S2 = Momentary Switch [package=ksa_sealed_tac_switch]
  S3 = Momentary Switch [package=ksa_sealed_tac_switch]
  J1 = Piezo Speaker

nets:
  N1: U2.GPIO32, S3.2
  N2: U2.GPIO33, S1.2
  GND: U2.GND, SERVO1.GND, S1.4, S3.4, J1.pin1
  VIN: U2.VIN, SERVO1.+5V
  N3: U2.GPIO2, LED1.anode
  N4: U2.GPIO16, LED2.anode
  N5: U2.GPIO17, SERVO1.Signal
  N6: U2.GPIO18, S2.1
  N7: U2.GPIO22, J1.pin2
  N8: LED1.cathode, LED2.cathode, S2.3

custom parts:
  ESP32S-HiLetgo: HiLetgo ESP-WROOM-32 ESP32 ESP-32S Development Board 2.4GHz Dual-Mode WiFi + Bluetooth Dual Cores Microcontroller The ESP32 integrated with Antenna switches, RF Balun, power amplifiers, low-noise amplifiers, filters, and management modules, and the entire solution occupies the least area of PCB. 2.4 GHz Wi-Fi plus Bluetooth dual-mode chip, with TSMC Ultra-low power consumption 40nm technology,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
  Tower Pro SG90 servo: Original file by John De Cristofaro http://www.adafruit.com/products/1449 Adafruit Feedback Servo (Small) Edited by: e-radionica.com 28/9/2015
