# Fritzing sketch HW04_12 (saved by Fritzing 0.9.3b)
breadboards: 3

parts:
  U1 = ESP32S-HiLetgo [part_number=ESP32S-HiLetgo]
  S3 = Momentary Switch [package=ksa_sealed_tac_switch]
  DI1 = 7-Segment LED Display [package=THT]
  LED1 = LED - 5mm [color="Red (633nm)" package="5 mm [THT]"]
  S4 = Momentary Switch [package=ksa_sealed_tac_switch]

nets:
  N1: U1.GPIO25, LED1.anode
  N2: U1.GPIO27, S4.3
  N3: U1.GND, DI1.commAnode#2
  N4: U1.GPIO13, S3.4
  N5: U1.GPIO4, DI1.cathodeE
  N6: U1.GPIO5, DI1.cathodeA
  N7: U1.GPIO18, DI1.cathodeB
  N8: U1.GPIO19, DI1.cathodeC
  N9: U1.GPIO21, DI1.cathodeDP
  N10: U1.GPIO3, DI1.cathodeD
  N11: U1.GPIO22, DI1.cathodeG
  N12: U1.GPIO23, DI1.cathodeF
  N13: S3.2, LED1.cathode

custom parts:
  ESP32S-HiLetgo: HiLetgo ESP-WROOM-32 ESP32 ESP-32S Development Board 2.4GHz Dual-Mode WiFi + Bluetooth Dual Cores Microcontroller The ESP32 integrated with Antenna switches, RF Balun, power amplifiers, low-noise amplifiers, filters, and management modules, and the entire solution occupies the least area of PCB. 2.4 GHz Wi-Fi plus Bluetooth dual-mode chip, with TSMC Ultra-low power consumption 40nm technology,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
