# Fritzing sketch HW05_12 (saved by Fritzing 0.9.3b)
breadboards: 2

parts:
  Grove1 = Grove OLED 128x96
  U1 = ESP32S-HiLetgo [part_number=ESP32S-HiLetgo]
  DI2 = 7-Segment LED Display [package=THT]
  S1 = Pushbutton [package="[THT]"]
  S2 = Pushbutton [package="[THT]"]

nets:
  GND: Grove1.GND, U1.GND, DI2.commAnode, DI2.cathodeF
  N1: Grove1.VCC, U1.3.3
  N2: Grove1.SDA, U1.GPIO21
  N3: Grove1.SCL, U1.GPIO22
  N4: U1.GPIO32, DI2.cathodeA
  N5: U1.GPIO25, DI2.cathodeG
  N6: U1.GPIO27, S2.Pin_3, S2.Pin_4
  N7: U1.GPIO13, S1.Pin_3, S1.Pin_4
  N8: U1.GPIO4, DI2.cathodeE
  N9: U1.GPIO18, DI2.cathodeB
  N10: U1.GPIO19, DI2.cathodeC
  N11: U1.GPIO3, DI2.cathodeD
  N12: S1.Pin_1, S1.Pin_2, S2.Pin_1, S2.Pin_2

custom parts:
  ESP32S-HiLetgo: HiLetgo ESP-WROOM-32 ESP32 ESP-32S Development Board 2.4GHz Dual-Mode WiFi + Bluetooth Dual Cores Microcontroller The ESP32 integrated with Antenna switches, RF Balun, power amplifiers, low-noise amplifiers, filters, and management modules, and the entire solution occupies the least area of PCB. 2.4 GHz Wi-Fi plus Bluetooth dual-mode chip, with TSMC Ultra-low power consumption 40nm technology,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
