# Fritzing sketch HW06_12 (saved by Fritzing 0.9.3b)
breadboards: 2

parts:
  U1 = ESP32S-HiLetgo [part_number=ESP32S-HiLetgo]
  Grove1 = Grove OLED 128x96
  R1 = Photocell (LDR) [package=THT]
  LED1 = smd LED [color="Red (633nm)" package="1206 [SMD]"]
  R2 = Resistor [tolerance=±5% resistance=220 package="0402 [SMD]"]

nets:
  N1: U1.3.3, Grove1.VCC, R2.Pin_0
  N2: U1.GPIO36, R1.pin_0, R2.Pin_1
  N3: U1.GPIO32, LED1.anode
  GND: U1.GND, Grove1.GND
  N4: U1.GPIO21, Grove1.SDA
  N5: U1.GPIO22, Grove1.SCL

custom parts:
  ESP32S-HiLetgo: HiLetgo ESP-WROOM-32 ESP32 ESP-32S Development Board 2.4GHz Dual-Mode WiFi + Bluetooth Dual Cores Microcontroller The ESP32 integrated with Antenna switches, RF Balun, power amplifiers, low-noise amplifiers, filters, and management modules, and the entire solution occupies the least area of PCB. 2.4 GHz Wi-Fi plus Bluetooth dual-mode chip, with TSMC Ultra-low power consumption 40nm technology,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
