# Fritzing sketch HW12 (saved by Fritzing 0.9.3b)
breadboards: 3

parts:
  元件1 = MQ-3 breakout
  U1 = ESP32S-HiLetgo [part_number=ESP32S-HiLetgo]
  R1 = Resistor [tolerance=±5% resistance=220 package="1206 [SMD]"]
  R2 = Resistor [tolerance=±5% resistance=220 package="1206 [SMD]"]
  S1 = Pushbutton [package="[THT]"]
  S2 = Pushbutton [package="[THT]"]
  LED1 = smd LED [color="Red (633nm)" package="0603 [SMD]"]
  R3 = Resistor [tolerance=±5% resistance=220 package="1206 [SMD]"]
  SERVO2 = Tower Pro SG90 servo [part_number=101246]
  R4 = Resistor [tolerance=±5% resistance=220 package="1206 [SMD]"]
  LED2 = smd LED [color="Blue (470nm)" package="0603 [SMD]"]
  DI2 = 7-Segment LED Display [package=THT]
  Grove1 = Grove OLED 128x96

nets:
  VCC: 元件1.VCC, U1.VIN, SERVO2.+5V
  GND: 元件1.GND, U1.GND, R1.Pin_0, SERVO2.GND, DI2.commAnode, Grove1.GND
  N1: 元件1.AO, R2.Pin_1
  N2: U1.3.3, Grove1.VCC
  N3: U1.GPIO36, R1.Pin_1, R2.Pin_0, LED1.cathode
  N4: U1.GPIO32, DI2.cathodeA
  N5: U1.GPIO25, DI2.cathodeG
  N6: U1.GPIO26, R4.Pin_0
  N7: U1.GPIO27, S2.Pin_3, S2.Pin_4
  N8: U1.GPIO13, S1.Pin_3, S1.Pin_4
  N9: U1.GPIO4, DI2.cathodeE
  N10: U1.GPIO16, R3.Pin_1
  N11: U1.GPIO17, SERVO2.Signal
  N12: U1.GPIO18, DI2.cathodeB
  N13: U1.GPIO19, DI2.cathodeC
  N14: U1.GPIO21, Grove1.SDA
  N15: U1.GPIO3, DI2.cathodeD
  N16: U1.GPIO22, Grove1.SCL
  N17: U1.GPIO23, DI2.cathodeF
  N18: S1.Pin_1, S1.Pin_2, S2.Pin_1, S2.Pin_2, LED2.cathode
  N19: LED1.anode, R3.Pin_0
  N20: R4.Pin_1, LED2.anode

custom parts:
  MQ-3 breakout: Alcohol sensor is capable of detecting alcohol (ethanol) particles on itself and gives the information in digital form back to us to manipulate with it. SKU:101251 • Voltage: 5V DC • Power: max 750mW • Measurement range: 0.04-4mg/L
  ESP32S-HiLetgo: HiLetgo ESP-WROOM-32 ESP32 ESP-32S Development Board 2.4GHz Dual-Mode WiFi + Bluetooth Dual Cores Microcontroller The ESP32 integrated with Antenna switches, RF Balun, power amplifiers, low-noise amplifiers, filters, and management modules, and the entire solution occupies the least area of PCB. 2.4 GHz Wi-Fi plus Bluetooth dual-mode chip, with TSMC Ultra-low power consumption 40nm technology,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
  Tower Pro SG90 servo: Original file by John De Cristofaro http://www.adafruit.com/products/1449 Adafruit Feedback Servo (Small) Edited by: e-radionica.com 28/9/2015
