# Fritzing sketch final_12 (saved by Fritzing 0.9.3b)
breadboards: 3

parts:
  U1 = ESP32S-HiLetgo [part_number=ESP32S-HiLetgo]
  LED1 = LED - 5mm [color="Red (633nm)" package="5 mm [THT]"]
  LED2 = LED - 5mm [color="Green (555nm)" package="5 mm [THT]"]
  hc-sr1 = hc-sr04
  J1 = Basic Servo
  C1 = Capacitor Polarized [package=cpol-radial-1000uf-25v]
  VCC1 = Battery
  S1 = Square Pushbutton
  R1 = Resistor [tolerance=±5% resistance=220 package="0402 [SMD]"]

nets:
  N1: U1.GPIO25, hc-sr1.Trig
  N2: U1.GPIO26, hc-sr1.Echo
  N3: U1.GPIO12, J1.pulse
  GND: U1.GND, LED1.cathode, LED2.cathode, LED2.anode, hc-sr1.GND, J1.gnd
  VCC: U1.VIN, hc-sr1.VCC, J1.vcc
  N4: U1.GPIO19, LED1.anode
  N5: C1.+, VCC1.+, S1.leg0
  N6: C1.-, VCC1.-, R1.Pin_1
  N7: S1.leg1, R1.Pin_0

custom parts:
  ESP32S-HiLetgo: HiLetgo ESP-WROOM-32 ESP32 ESP-32S Development Board 2.4GHz Dual-Mode WiFi + Bluetooth Dual Cores Microcontroller The ESP32 integrated with Antenna switches, RF Balun, power amplifiers, low-noise amplifiers, filters, and management modules, and the entire solution occupies the least area of PCB. 2.4 GHz Wi-Fi plus Bluetooth dual-mode chip, with TSMC Ultra-low power consumption 40nm technology,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
